// Logisim project ALSU.circ as structural Verilog: 22 circuits, main circuit ALSU
module ALSU (
  input  [4:0] flags_in,
  input  [15:0] Ra,
  input  [15:0] Rb,
  input  [15:0] Rd,
  input  [15:0] instruction,
  output [15:0] result,
  output [4:0] f_out
);

  ALSU_body alsu_body_1 (
    .flags_in(flags_in), .Ra(Ra), .Rb(Rb), .Rd(Rd), .instruction(instruction), .result(result), .f_out(f_out));
endmodule

module logical_or (
  input  [15:0] in_1,
  input  [15:0] in_2,
  output [15:0] out_3
);

  assign out_3 = in_1 | in_2;  // OR_Gate or_1, 16 bits wide
endmodule

module logical_and (
  input  [15:0] in_1,
  input  [15:0] in_2,
  output [15:0] out_3
);

  assign out_3 = in_1 & in_2;  // AND_Gate and_1, 16 bits wide
endmodule

module logical_xor (
  input  [15:0] in_1,
  input  [15:0] in_2,
  output [15:0] out_3
);

  assign out_3 = in_1 ^ in_2;  // XOR_Gate xor_1, 16 bits wide
endmodule

module LU (
  input  [15:0] Ra,
  input  [15:0] Rb,
  input  [3:0] opcode,
  input  [4:0] f_in,
  output [15:0] result,
  output [4:0] f_out
);

  wire [15:0] a, o, x;

  logical_and logical_and_1 (.in_1(Ra), .in_2(Rb), .out_3(a));
  logical_or logical_or_1 (.in_1(Ra), .in_2(Rb), .out_3(o));
  logical_xor logical_xor_1 (.in_1(Ra), .in_2(Rb), .out_3(x));
  LU_output lu_output_1 (.l_and(a), .l_or(o), .l_xor(x), .opcode(opcode), .f_in(f_in), .result(result), .f_out(f_out));

  // Other names for the same wires on the sheet: op[3:0] = opcode
endmodule

module LU_output (
  input  [15:0] l_and,
  input  [15:0] l_or,
  input  [15:0] l_xor,
  input  [3:0] opcode,
  input  [4:0] f_in,
  output [15:0] result,
  output [4:0] f_out
);

  Multiplexer #(.select(4), .width(16)) multiplexer_1 (
    .in8(l_and), .in9(l_or), .in13(l_xor), .out(result), .sel(opcode));  // open: in0, in1, in2, in3, in4, in5, in6, in7, in10, in11, in12, in14, in15
  Comparator #(.width(16)) comparator_1 (.a(result), .b({16{1'b0}}), .eq(f_out[1]), .lt(f_out[0]));  // open: gt

  assign f_out[4:2] = f_in[4:2];
endmodule

module add_sub (
  input  [4:0] f_in,
  input  [15:0] Ra,
  input  [15:0] Rb,
  input  [3:0] opcode,
  output [15:0] result,
  output [4:0] f_out
);

  wire AddCarry, adder_2_cout, AddOverflow, and_1_out, and_2_out, comparator_1_eq, comparator_1_gt,
       not_1_out, not_2_out, subCarry, SubOverflow, subtractor_1_bout, subtractor_2_bout;
  wire [0:0] adder_1_out;
  wire [1:1] comparator_2_eq;
  wire [14:0] adder_2_out, subtractor_1_out;
  wire [15:15] subtractor_2_out;

  Comparator #(.mode("unsigned"), .width(16)) comparator_1 (
    .a(Ra), .b(Rb), .gt(comparator_1_gt), .eq(comparator_1_eq));  // open: lt
  not not_1 (not_1_out, f_in[4]);
  or or_1 (subCarry, comparator_1_gt, comparator_1_eq);
  not not_2 (not_2_out, f_in[4]);
  Comparator #(.width(16)) comparator_2 (.a({16{1'b0}}), .b(result), .eq(comparator_2_eq[1]));  // open: gt, lt
  and and_1 (and_1_out, not_1_out, f_in[3]);
  and and_2 (and_2_out, f_in[3], not_2_out);
  Adder #(.width(1)) adder_1 (.a(Ra[15]), .b(Rb[15]), .out(adder_1_out[0]), .cout(AddCarry));  // open: cin
  Adder #(.width(15)) adder_2 (.a(Ra[14:0]), .b(Rb[14:0]), .out(adder_2_out), .cin(and_1_out), .cout(adder_2_cout));
  Subtractor #(.width(15)) subtractor_1 (
    .a(Ra[14:0]), .b(Rb[14:0]), .out(subtractor_1_out), .bin(and_2_out), .bout(subtractor_1_bout));
  Subtractor #(.width(1)) subtractor_2 (
    .a(Ra[15]), .b(Rb[15]), .out(subtractor_2_out[15]), .bout(subtractor_2_bout));  // open: bin
  xor xor_1 (SubOverflow, subtractor_2_bout, subtractor_1_bout);
  Multiplexer #(.select(4), .width(16)) multiplexer_1 (
    .in10({adder_2_out, adder_1_out[0]}), .in11({subtractor_2_out[15], subtractor_1_out}), .out(result),
    .sel(opcode));  // open: in0, in1, in2, in3, in4, in5, in6, in7, in8, in9, in12, in13, in14, in15
  xor xor_2 (AddOverflow, adder_2_cout, AddCarry);
  Multiplexer #(.select(4), .width(5)) multiplexer_2 (
    .in10({f_in[4], AddCarry, AddOverflow, comparator_2_eq[1], result[15]}),
    .in11({f_in[4], subCarry, SubOverflow, comparator_2_eq[1], result[15]}), .out(f_out), .sel(opcode));  // open: in0, in1, in2, in3, in4, in5, in6, in7, in8, in9, in12, in13, in14, in15

  // Other names for the same wires on the sheet: SFlag = result[15]; CB = f_in[4]; op[3:0] = opcode;
  //   RaLastBit = Ra[15]; RbLastBit = Rb[15]
endmodule

module overflow_detection (
  input  [15:0] Ra,
  input  [15:0] Rb,
  input  sub,
  input  [15:0] result,
  output overflow
);

  wire xnor_1_out, xor_1_out, xor_2_out;

  xor xor_1 (xor_1_out, Rb[15], sub);
  xnor xnor_1 (xnor_1_out, Ra[15], xor_1_out);
  xor xor_2 (xor_2_out, xor_1_out, result[15]);
  and and_1 (overflow, xnor_1_out, xor_2_out);

  // Other names for the same wires on the sheet: a15 = Ra[15]; b15 = Rb[15]; r15 = result[15]

  // Notes on the sheet:
  //   check if a15and b15 is the same
  //   if it's subtraction we flip the b15
  //   overflow detection
  //   two conditions should be both fulfilled
  //   check one of them is the same with the result
endmodule

module mul (
  input  [4:0] f_in,
  input  [15:0] Ra,
  input  [15:0] Rb,
  output [15:0] result,
  output [4:0] f_out
);

  wire multiplexer_1_out, not_1_out;
  wire [15:0] bit_extender_1_out, multiplexer_2_out, multiplier_1_cout, multiplier_1_out;

  Multiplexer #(.enable("true")) multiplexer_1 (
    .in0(f_in[3]), .in1(1'b0), .out(multiplexer_1_out), .sel(f_in[4]));  // open: en
  assign bit_extender_1_out = {{15{multiplexer_1_out}}, multiplexer_1_out};  // Bit_Extender bit_extender_1
  Multiplier #(.width(16)) multiplier_1 (
    .a(Ra), .b(Rb), .out(multiplier_1_out), .cin(bit_extender_1_out), .cout(multiplier_1_cout));
  Multiplexer #(.enable("true"), .select(4), .width(16)) multiplexer_2 (
    .in0(multiplier_1_out), .in8(multiplier_1_cout), .out(multiplexer_2_out), .sel(f_in[3:0]));  // open: in1, in2, in3, in4, in5, in6, in7, in9, in10, in11, in12, in13, in14, in15, en
  Multiplexer #(.enable("true"), .width(16)) multiplexer_3 (
    .in0(multiplier_1_out), .in1(multiplexer_2_out), .out(result), .sel(not_1_out));  // open: en
  not not_1 (not_1_out, f_in[4]);
  Comparator #(.width(16)) comparator_1 (.a(multiplier_1_cout), .b({16{1'b0}}), .gt(f_out[3]));  // open: eq, lt
  Comparator #(.width(16)) comparator_2 (.a(result), .b({16{1'b0}}), .eq(f_out[1]), .lt(f_out[0]));  // open: gt
  overflow_detection overflow_detection_1 (.Ra(Ra), .Rb(Rb), .sub(1'b0), .result(result), .overflow(f_out[2]));

  assign f_out[4] = f_in[4];

  // Other names for the same wires on the sheet: CB = f_in[4]; other_4flags[3:0] = f_in[3:0]

  // Notes on the sheet:
  //   carry-in
  //   if CB on we take lower 16 bit of the result
endmodule

module ASR (
  input  [4:0] flags,
  input  [15:0] Rb,
  output [4:0] f_out,
  output [15:0] result
);

  Shifter #(.shift("ar"), .width(16)) shifter_1 (.in(Rb), .\dist (4'b0001), .out(result));
  Comparator #(.width(16)) comparator_1 (.a(result), .b({16{1'b0}}), .eq(f_out[1]), .lt(f_out[0]));  // open: gt

  assign f_out[4:2] = {flags[4], Rb[0], flags[2]};

  // Other names for the same wires on the sheet: bit_shift_out = Rb[0]

  // Notes on the sheet:
  //   the bit got shifted out is the new carry
  //   ASR igores incoming carry, always producing a result that's half of the signed value
endmodule

module ASL (
  input  [4:0] flags,
  input  [15:0] Rb,
  output [4:0] f_out,
  output [15:0] result
);

  wire [15:0] add_result;

  and and_1 (result[0], Rb[14], ~flags[4]);  // AND_Gate
  Comparator #(.width(16)) comparator_1 (
    .a({Rb[15], Rb[13:0], result[0]}), .b({16{1'b0}}), .eq(f_out[1]), .lt(f_out[0]));  // open: gt
  add_sub add (.f_in(flags), .Ra(Rb), .Rb(Rb), .opcode(4'b1000), .result(add_result));  // open: f_out
  overflow_detection overflow (.Ra(Rb), .Rb(Rb), .sub(1'b0), .result(add_result), .overflow(f_out[2]));

  assign f_out[4:3] = {flags[4], Rb[14]};
  assign result[15:1] = {Rb[15], Rb[13:0]};

  // Other names for the same wires on the sheet: f_in[4:0] = flags; v = f_out[2]

  // Notes on the sheet:
  //   signed
  //   this basically shifts all the digits left by one
  //   then, the value of C ^ F4' will be in the least significant bit 
  //   all comparator like this is to decide the sign and zero flags output
endmodule

module LSR (
  input  [4:0] flags,
  input  [15:0] Rb,
  output [4:0] f_out,
  output [15:0] result
);

  and and_1 (result[15], Rb[0], ~flags[4]);  // AND_Gate
  Comparator #(.width(16)) comparator_1 (
    .a({result[15], Rb[15:1]}), .b({16{1'b0}}), .eq(f_out[1]), .lt(f_out[0]));  // open: gt

  assign f_out[4:2] = {flags[4], Rb[0], flags[2]};
  assign result[14:0] = Rb[15:1];

  // Other names for the same wires on the sheet: f_in[4:0] = flags

  // Notes on the sheet:
  //   Similar to LSL, this shift the digits in a reverse way
endmodule

module LSL8 (
  input  [4:0] flags,
  input  [15:0] Rb,
  output [4:0] f_out,
  output [15:0] result
);

  Comparator #(.width(16)) comparator_1 (
    .a({Rb[7:0], {8{1'b0}}}), .b({16{1'b0}}), .eq(f_out[1]), .lt(f_out[0]));  // open: gt

  assign f_out[4:2] = flags[4:2];
  assign result = {Rb[7:0], {8{1'b0}}};

  // Notes on the sheet:
  //   LSL8 instruction
  //   the eight-bit shift operations shift in zeros, regardless of the carry-blog(F4) flag.
endmodule

module LSR8 (
  input  [4:0] flags,
  input  [15:0] Rb,
  output [4:0] f_out,
  output [15:0] result
);

  Comparator #(.width(16)) comparator_1 (
    .a({{8{1'b0}}, Rb[15:8]}), .b({16{1'b0}}), .eq(f_out[1]), .lt(f_out[0]));  // open: gt

  assign f_out[4:2] = flags[4:2];
  assign result = {{8{1'b0}}, Rb[15:8]};

  // Notes on the sheet:
  //   LSR8 instruction
  //   the eight-bit shift operations shift in zeros, regardless of the carry-blog(F4) flag.
endmodule

module DEC (
  input  [4:0] flags_in,
  input  [15:0] Rb,
  input  [3:0] b0_3,
  input  [3:0] b4_7,
  output [4:0] flags_out,
  output [15:0] result
);

  wire [15:0] adder_1_out, bit_extender_1_out;

  assign bit_extender_1_out = {{10{b4_7[1]}}, {b4_7[1:0], b0_3}};  // Bit_Extender bit_extender_1
  Adder #(.width(16)) adder_1 (.a(bit_extender_1_out), .b(16'h1), .out(adder_1_out));  // open: cin, cout
  Subtractor #(.width(16)) subtractor_1 (.a(Rb), .b(adder_1_out), .out(result), .bout(flags_out[3]));  // open: bin
  Comparator #(.width(16)) comparator_1 (.a(result), .b({16{1'b0}}), .eq(flags_out[1]), .lt(flags_out[0]));  // open: gt

  assign {flags_out[4], flags_out[2]} = {flags_in[4], flags_in[2]};

  // Notes on the sheet:
  //   default dec/inc by 1
  //   b0_5 as delta
  //   inc/dec ignores incoming carry
endmodule

module INC (
  input  [4:0] flags_in,
  input  [15:0] Rb,
  input  [3:0] b0_3,
  input  [3:0] b4_7,
  output [4:0] flags_out,
  output [15:0] result
);

  wire [15:0] adder_1_out, bit_extender_1_out;

  assign bit_extender_1_out = {{10{b4_7[1]}}, {b4_7[1:0], b0_3}};  // Bit_Extender bit_extender_1
  Adder #(.width(16)) adder_1 (.a(bit_extender_1_out), .b(16'h1), .out(adder_1_out));  // open: cin, cout
  Adder #(.width(16)) adder_2 (.a(Rb), .b(adder_1_out), .out(result), .cout(flags_out[3]));  // open: cin
  Comparator #(.width(16)) comparator_1 (.a(result), .b({16{1'b0}}), .eq(flags_out[1]), .lt(flags_out[0]));  // open: gt

  assign {flags_out[4], flags_out[2]} = {flags_in[4], flags_in[2]};
endmodule

module ALSU_body (
  input  [4:0] flags_in,
  input  [15:0] Ra,
  input  [15:0] Rb,
  input  [15:0] Rd,
  input  [15:0] instruction,
  output [15:0] result,
  output [4:0] f_out
);

  wire [4:0] asf, Luf, mulf, shiftf;
  wire [15:0] lu_1_result, mul_1_result, sethi_1_result, setlo_1_result, shifts_1_result, undriven;

  shifts shifts_1 (
    .flags_in(flags_in), .Rb(Rb), .Rd(Rd), .b0_3(instruction[3:0]), .b4_7(instruction[7:4]),
    .b8_11(instruction[11:8]), .result(shifts_1_result), .f_out(shiftf));
  LU lu_1 (.Ra(Ra), .Rb(Rb), .opcode(instruction[15:12]), .f_in(flags_in), .result(lu_1_result), .f_out(Luf));
  add_sub add_sub_1 (.f_in(flags_in), .Ra(Ra), .Rb(Rb), .opcode(instruction[15:12]), .f_out(asf));  // open: result
  mul mul_1 (.f_in(flags_in), .Ra(Ra), .Rb(Rb), .result(mul_1_result), .f_out(mulf));
  SETLO setlo_1 (.b0_3(instruction[3:0]), .b4_7(instruction[7:4]), .result(setlo_1_result));
  SETHI sethi_1 (.Rb(Rd), .b0_3(instruction[3:0]), .b4_7(instruction[7:4]), .result(sethi_1_result));
  Multiplexer #(.select(4), .width(16)) multiplexer_1 (
    .in3(shifts_1_result), .in8(lu_1_result), .in9(lu_1_result), .in10(undriven), .in11(undriven),
    .in12(mul_1_result), .in13(lu_1_result), .in14(setlo_1_result), .in15(sethi_1_result), .out(result),
    .sel(instruction[15:12]));  // open: in0, in1, in2, in4, in5, in6, in7
  Multiplexer #(.select(4), .width(5)) multiplexer_2 (
    .in0(flags_in), .in1(flags_in), .in2(flags_in), .in3(shiftf), .in4(flags_in), .in5(flags_in),
    .in6(flags_in), .in7(flags_in), .in8(Luf), .in9(Luf), .in10(asf), .in11(asf), .in12(mulf), .in13(Luf),
    .in14(flags_in), .in15(flags_in), .out(f_out), .sel(instruction[15:12]));

  // Other names for the same wires on the sheet: b0_3[3:0] = instruction[3:0]; b4_7[3:0] = instruction[7:4];
  //   b8_11[3:0] = instruction[11:8]; f_in[4:0] = flags_in; opc[3:0] = instruction[15:12]

  // Notes on the sheet:
  //   each instruction has their respective flag_in and flag_out 
  //   the multiplexer will base on the opcode to select a result flag_out
  //   This also means each time we change all five flags together
  //   CALL/RETURN do not change flags
  //   LOAD does not modify flags, STORE changes s and z
  //   (but for now just output same flags, will change in memory circuit)
  //   SETHI and SETLO doesn't affect flags, so the flags in goes right in here
endmodule

module shifts (
  input  [4:0] flags_in,
  input  [15:0] Rb,
  input  [15:0] Rd,
  input  [3:0] b0_3,
  input  [3:0] b4_7,
  input  [3:0] b8_11,
  output [15:0] result,
  output [4:0] f_out
);

  wire [4:0] ASLf, ASRf, DECf, flagsf, INCf, LSL8f, LSLf, LSR8f, LSRf;
  wire [15:0] ASLr, ASRr, DECr, flagsr, INCr, LSL8r, LSLr, LSR8r, LSRr;

  LSL lsl_1 (.flags(flags_in), .Rb(Rb), .f_out(LSLf), .result(LSLr));
  LSR lsr_1 (.flags(flags_in), .Rb(Rb), .f_out(LSRf), .result(LSRr));
  LSL8 lsl8_1 (.flags(flags_in), .Rb(Rb), .f_out(LSL8f), .result(LSL8r));
  LSR8 lsr8_1 (.flags(flags_in), .Rb(Rb), .f_out(LSR8f), .result(LSR8r));
  ASL asl_1 (.flags(flags_in), .Rb(Rb), .f_out(ASLf), .result(ASLr));
  ASR asr_1 (.flags(flags_in), .Rb(Rb), .f_out(ASRf), .result(ASRr));
  INC inc_1 (.flags_in(flags_in), .Rb(Rd), .b0_3(b0_3), .b4_7(b4_7), .flags_out(INCf), .result(INCr));
  DEC dec_1 (.flags_in(flags_in), .Rb(Rd), .b0_3(b0_3), .b4_7(b4_7), .flags_out(DECf), .result(DECr));
  flags flags_1 (.flags_in(flags_in), .b0_3(b0_3), .b8_11(b8_11), .flags_out(flagsf), .result(flagsr));
  Multiplexer #(.select(4), .width(16)) multiplexer_1 (
    .in0(LSLr), .in1(LSRr), .in2(LSL8r), .in3(LSR8r), .in4(ASLr), .in5(ASRr), .in7(flagsr), .in8(INCr),
    .in9(INCr), .in10(INCr), .in11(INCr), .in12(DECr), .in13(DECr), .in14(DECr), .in15(DECr), .out(result),
    .sel(b4_7));  // open: in6
  Multiplexer #(.select(4), .width(5)) multiplexer_2 (
    .in0(LSLf), .in1(LSRf), .in2(LSL8f), .in3(LSR8f), .in4(ASLf), .in5(ASRf), .in6(flagsf), .in7(flags_in),
    .in8(INCf), .in9(INCf), .in10(INCf), .in11(INCf), .in12(DECf), .in13(DECf), .in14(DECf), .in15(DECf),
    .out(f_out), .sel(b4_7));

  // Other names for the same wires on the sheet: f_in[4:0] = flags_in

  // Notes on the sheet:
  //   all the "3" instructions, shifts, direct flag changes and INC/DEC
endmodule

module LSL (
  input  [4:0] flags,
  input  [15:0] Rb,
  output [4:0] f_out,
  output [15:0] result
);

  Shifter #(.width(16)) shifter_1 (.in(Rb), .\dist (4'b0001), .out(result));
  Comparator #(.width(16)) comparator_1 (.a(result), .b({16{1'b0}}), .eq(f_out[1]), .lt(f_out[0]));  // open: gt

  assign f_out[4:2] = {flags[4], Rb[15], flags[2]};

  // Notes on the sheet:
  //   this basically shifts all the digits left by one
  //   then, the value of C ^ F4' will be in the least significant bit 
  //   all comparator like this is to decide the sign and zero flags output
  //   c became the bit that's shifted out
endmodule

module flags (
  input  [4:0] flags_in,
  input  [3:0] b0_3,
  input  [3:0] b8_11,
  output [4:0] flags_out,
  output [15:0] result
);

  wire [4:0] FOFF, FON;
  wire [15:0] bit_extender_1_out, Rb;

  assign FON = flags_in | {b8_11[0], b0_3};  // OR_Gate or_1, 5 bits wide
  assign FOFF = flags_in & ~{b8_11[0], b0_3};  // AND_Gate and_1, 5 bits wide
  assign bit_extender_1_out = {{11{flags_in[4]}}, flags_in};  // Bit_Extender bit_extender_1
  Multiplexer #(.enable("true"), .width(16)) multiplexer_1 (
    .in0(bit_extender_1_out), .in1(Rb), .out(result), .sel(b0_3[3]));  // open: en
  Multiplexer #(.enable("true"), .select(3), .width(5)) multiplexer_2 (
    .in0(FON), .in2({b8_11[0], b0_3}), .in4(FOFF), .in6({flags_in[4], b0_3}), .out(flags_out),
    .sel(b8_11[3:1]));  // open: in1, in3, in5, in7, en

  // Other names for the same wires on the sheet: b9_11[2:0] = b8_11[3:1]; f_in[4:0] = flags_in; b8 = b8_11[0];
  //   v[4:0] = {b8_11[0], b0_3}; v_2[4:0] = {flags_in[4], b0_3}; c_block = flags_in[4]

  // Notes on the sheet:
  //   SET flag instructions depend on b9-11
  //   an or gate will turn on flags accordingly with 1
  //   this will turn off flags that the value says 1
endmodule

module SETLO (
  input  [3:0] b0_3,
  input  [3:0] b4_7,
  output [15:0] result
);

  assign result = {{8{b4_7[3]}}, {b4_7, b0_3}};  // Bit_Extender bit_extender_1
endmodule

module SETHI (
  input  [15:0] Rb,
  input  [3:0] b0_3,
  input  [3:0] b4_7,
  output [15:0] result
);

  Bit_Extender #(.in_width(16), .out_width(8)) bit_extender_1 (.in(Rb), .out(result[7:0]));

  assign result[15:8] = {b4_7, b0_3};
endmodule
